# Fritzing sketch prog08 (saved by Fritzing 0.9.4)
breadboards: 1

parts:
  S1 = Pushbutton [package="[THT]"]
  S2 = Pushbutton [package="[THT]"]
  S3 = Pushbutton [package="[THT]"]
  Raspberry_Pi_1 = Raspberry Pi 3 [part_number=RPI-3-V1.2]

nets:
  N1: S1.Pin_1, S1.Pin_2, Raspberry_Pi_1.GPIO2
  N2: S1.Pin_3, S1.Pin_4, S2.Pin_3, S2.Pin_4, S3.Pin_3, S3.Pin_4, Raspberry_Pi_1.GND
  N3: S2.Pin_1, S2.Pin_2, Raspberry_Pi_1.GPIO3
  N4: S3.Pin_1, S3.Pin_2, Raspberry_Pi_1.GPIO17

notes:
  Right
  Up/Down
  Left
