# Fritzing sketch prog03 (saved by Fritzing 0.9.4)
breadboards: 1

parts:
  Raspberry_Pi_1 = Raspberry Pi 3 [part_number=RPI-3-V1.2]
  LED1 = smd LED [color="Red (633nm)" package="0603 [SMD]"]
  R1 = Resistor [tolerance=±5% resistance=220 package="0402 [SMD]"]
  LED2 = smd LED [color="Yellow (595nm)" package="0603 [SMD]"]
  LED3 = smd LED [color="Green (555nm)" package="0603 [SMD]"]
  R2 = Resistor [tolerance=±5% resistance=220 package="0402 [SMD]"]
  R3 = Resistor [tolerance=±5% resistance=220 package="0402 [SMD]"]

nets:
  N1: Raspberry_Pi_1.GPIO17, LED1.anode
  N2: Raspberry_Pi_1.GPIO27, LED2.anode
  N3: Raspberry_Pi_1.GPIO22, LED3.anode
  N4: Raspberry_Pi_1.GND, R1.Pin_1, R2.Pin_1, R3.Pin_1
  N5: LED1.cathode, R1.Pin_0
  N6: LED2.cathode, R2.Pin_0
  N7: LED3.cathode, R3.Pin_0
