# Fritzing sketch prog04 (saved by Fritzing 0.9.4)
breadboards: 1

parts:
  Raspberry_Pi_1 = Raspberry Pi 3 [part_number=RPI-3-V1.2]
  R1 = Resistor [tolerance=±5% resistance=220 package="0402 [SMD]"]
  R2 = Resistor [tolerance=±5% resistance=220 package="0402 [SMD]"]
  R3 = Resistor [tolerance=±5% resistance=220 package="0402 [SMD]"]
  LED1 = RGB LED (com. anode, rbg) [package="5 mm [THT]"]

nets:
  N1: Raspberry_Pi_1.GPIO17, R1.Pin_1
  N2: Raspberry_Pi_1.GPIO27, R2.Pin_1
  N3: Raspberry_Pi_1.GPIO22, R3.Pin_1
  N4: Raspberry_Pi_1.GND, LED1.common_anode
  N5: R1.Pin_0, LED1.red_cathode
  N6: R2.Pin_0, LED1.blue_cathode
  N7: R3.Pin_0, LED1.green_cathode
