# Fritzing sketch prog041 (saved by Fritzing 0.9.4)
breadboards: 1

parts:
  Raspberry_Pi_1 = Raspberry Pi 3 [part_number=RPI-3-V1.2]
  R1 = Resistor [tolerance=±5% resistance=220 package="0402 [SMD]"]
  R2 = Resistor [tolerance=±5% resistance=220 package="0402 [SMD]"]
  R3 = Resistor [tolerance=±5% resistance=220 package="0402 [SMD]"]
  LED1 = RGB LED (com. anode, rbg) [package="5 mm [THT]"]
  S1 = Pushbutton [package="[THT]"]
  S2 = Pushbutton [package="[THT]"]
  S3 = Pushbutton [package="[THT]"]

nets:
  N1: Raspberry_Pi_1.GPIO2, S1.Pin_3, S1.Pin_4
  N2: Raspberry_Pi_1.GPIO3, S2.Pin_3, S2.Pin_4
  N3: Raspberry_Pi_1.GPIO17, S3.Pin_3, S3.Pin_4
  N4: Raspberry_Pi_1.GPIO10, R1.Pin_1
  N5: Raspberry_Pi_1.GPIO9, R2.Pin_1
  N6: Raspberry_Pi_1.GPIO11, R3.Pin_1
  N7: Raspberry_Pi_1.GND, LED1.common_anode, S1.Pin_1, S1.Pin_2, S2.Pin_1, S2.Pin_2, S3.Pin_1, S3.Pin_2
  N8: R1.Pin_0, LED1.red_cathode
  N9: R2.Pin_0, LED1.blue_cathode
  N10: R3.Pin_0, LED1.green_cathode
