# Fritzing sketch prog06 (saved by Fritzing 0.9.4)
breadboards: 1

parts:
  Raspberry_Pi_1 = Raspberry Pi 3 [part_number=RPI-3-V1.2]
  LED1 = smd LED [color="Red (633nm)" package="0603 [SMD]"]
  S1 = Pushbutton [package="[SMD]"]
  R1 = Resistor [tolerance=±5% resistance=220 package="0402 [SMD]"]
  S2 = Pushbutton [package="[SMD]"]
  R2 = Resistor [tolerance=±5% resistance=220 package="0402 [SMD]"]
  LED2 = smd LED [color="Red (633nm)" package="0805 [SMD]"]
  LED2_2 = smd LED [color="Blue (505nm)" package="1206 [SMD]"]

nets:
  N1: Raspberry_Pi_1.GPIO2, S1.Pin_3, S1.Pin_4
  N2: Raspberry_Pi_1.GPIO3, S2.Pin_3, S2.Pin_4
  N3: Raspberry_Pi_1.GPIO10, R1.Pin_0
  N4: Raspberry_Pi_1.GPIO9, R2.Pin_0
  N5: Raspberry_Pi_1.GND, LED1.cathode, S1.Pin_1, S1.Pin_2, S2.Pin_1, S2.Pin_2, LED2.cathode, LED2_2.cathode
  N6: LED1.anode, R1.Pin_1
  N7: R2.Pin_1, LED2.anode, LED2_2.anode
