# Fritzing sketch prog00_schema (saved by Fritzing 0.9.4)
breadboards: 1

parts:
  Raspberry_Pi_1 = Raspberry Pi 3 [part_number=RPI-3-V1.2]
  IC1 = L293D [package=THT]
  M1 = DC Motor
  VCC1 = 4 x AAA Battery Mount

nets:
  N1: Raspberry_Pi_1.GIPO25, IC1.Enable_1
  N2: Raspberry_Pi_1.GIPO24, IC1.In_1
  N3: Raspberry_Pi_1.GIPO23, IC1.In_2
  N4: Raspberry_Pi_1.GND, IC1.0V, VCC1.-
  N5: Raspberry_Pi_1.5V, IC1.+V
  N6: IC1.Out_1_(_Controlled_by_Enable_1_), M1.pin_2
  N7: IC1.Out_2_(_Controlled_by_Enable_1_), M1.pin_1
  N8: IC1.+Vmotor, VCC1.+
