# Fritzing sketch prog01_schema (saved by Fritzing 0.9.4)
breadboards: 1

parts:
  Raspberry_Pi_1 = Raspberry Pi 3 [part_number=RPI-3-V1.2]
  IC1 = L293D [package=THT]
  M1 = DC Motor
  VCC1 = 4 x AAA Battery Mount
  S1 = Pushbutton [package="[THT]"]
  S2 = Pushbutton [package="[THT]"]

nets:
  N1: Raspberry_Pi_1.GIPO17, S2.Pin_1, S2.Pin_2
  N2: Raspberry_Pi_1.GIPO27, S1.Pin_3, S1.Pin_4
  N3: Raspberry_Pi_1.GND, IC1.0V, VCC1.-, S1.Pin_1, S1.Pin_2, S2.Pin_3, S2.Pin_4
  N4: Raspberry_Pi_1.GIPO25, IC1.Enable_1
  N5: Raspberry_Pi_1.GIPO24, IC1.In_1
  N6: Raspberry_Pi_1.GIPO23, IC1.In_2
  N7: Raspberry_Pi_1.5V, IC1.+V
  N8: IC1.Out_1_(_Controlled_by_Enable_1_), M1.pin_2
  N9: IC1.Out_2_(_Controlled_by_Enable_1_), M1.pin_1
  N10: IC1.+Vmotor, VCC1.+
