# Fritzing sketch prog02_schema (saved by Fritzing 0.9.4)
breadboards: 1

parts:
  Raspberry_Pi_1 = Raspberry Pi 3 [part_number=RPI-3-V1.2]
  IC1 = L293D [package=THT]
  M1 = DC Motor
  VCC1 = 4 x AAA Battery Mount
  S1 = Pushbutton [package="[THT]"]
  S2 = Pushbutton [package="[THT]"]
  S3 = Pushbutton [package="[THT]"]
  LED1 = RGB LED (com. cathode, rgb) [package="5 mm [THT]"]
  R1 = Resistor [tolerance=±5% resistance=220 package=THT]
  R2 = Resistor [tolerance=±5% resistance=220 package=THT]
  R3 = Resistor [tolerance=±5% resistance=220 package=THT]

nets:
  N1: Raspberry_Pi_1.GIPO17, S2.Pin_1, S2.Pin_2
  N2: Raspberry_Pi_1.GIPO27, S1.Pin_3, S1.Pin_4
  N3: Raspberry_Pi_1.GIPO22, S3.Pin_3, S3.Pin_4
  N4: Raspberry_Pi_1.GIPO10, LED1.green_anode, R2.Pin_0, R2.Pin_1
  N5: Raspberry_Pi_1.GIPO9, LED1.red_anode, R1.Pin_0, R1.Pin_1
  N6: Raspberry_Pi_1.GIPO11, LED1.blue_anode, R3.Pin_0, R3.Pin_1
  N7: Raspberry_Pi_1.GIPO25, IC1.Enable_1
  N8: Raspberry_Pi_1.GIPO24, IC1.In_1
  N9: Raspberry_Pi_1.GIPO23, IC1.In_2
  N10: Raspberry_Pi_1.GND, IC1.0V, VCC1.-, S1.Pin_1, S1.Pin_2, S2.Pin_3, S2.Pin_4, S3.Pin_1, S3.Pin_2, LED1.common_cathode
  N11: Raspberry_Pi_1.5V, IC1.+V
  N12: IC1.Out_1_(_Controlled_by_Enable_1_), M1.pin_2
  N13: IC1.Out_2_(_Controlled_by_Enable_1_), M1.pin_1
  N14: IC1.+Vmotor, VCC1.+
