# Fritzing sketch prog04_schema (saved by Fritzing 0.9.4)
breadboards: 1

parts:
  Raspberry_Pi_1 = Raspberry Pi 3 [part_number=RPI-3-V1.2]
  IC1 = L293D [package=THT]
  M1 = DC Motor
  VCC1 = 4 x AAA Battery Mount
  S1 = Pushbutton [package="[THT]"]
  S2 = Pushbutton [package="[THT]"]
  S3 = Pushbutton [package="[THT]"]
  S4 = Pushbutton [package="[THT]"]
  M2 = DC Motor

nets:
  N1: Raspberry_Pi_1.GIPO10, IC1.In_4
  N2: Raspberry_Pi_1.GIPO9, IC1.In_3
  N3: Raspberry_Pi_1.GIPO11, IC1.Enable_2
  N4: Raspberry_Pi_1.GIPO21, S3.Pin_3, S3.Pin_4
  N5: Raspberry_Pi_1.GIPO25, IC1.Enable_1
  N6: Raspberry_Pi_1.GIPO24, IC1.In_1
  N7: Raspberry_Pi_1.GIPO23, IC1.In_2
  N8: Raspberry_Pi_1.GND, IC1.0V, VCC1.-, S1.Pin_1, S1.Pin_2, S2.Pin_3, S2.Pin_4, S3.Pin_1, S3.Pin_2, S4.Pin_1, S4.Pin_2
  N9: Raspberry_Pi_1.GIPO18, S2.Pin_1, S2.Pin_2
  N10: Raspberry_Pi_1.GIPO15, S1.Pin_3, S1.Pin_4
  N11: Raspberry_Pi_1.GIPO14, S4.Pin_3, S4.Pin_4
  N12: Raspberry_Pi_1.5V, IC1.+V
  N13: IC1.Out_1_(_Controlled_by_Enable_1_), M1.pin_2
  N14: IC1.Out_2_(_Controlled_by_Enable_1_), M1.pin_1
  N15: IC1.+Vmotor, VCC1.+
  N16: IC1.Out_3_(_Controlled_by_Enable_2_), M2.pin_2
  N17: IC1.Out_4_(_Controlled_by_Enable_2_), M2.pin_1
