# Fritzing sketch prog05_schema (saved by Fritzing 0.9.4)
breadboards: 1

parts:
  Raspberry_Pi_1 = Raspberry Pi 3 [part_number=RPI-3-V1.2]
  J1 = Basic Servo
  VCC1 = 4 x AAA Battery Mount
  S1 = Momentary Switch [package=ksa_sealed_tac_switch]

nets:
  N1: Raspberry_Pi_1.GPIO22, S1.3, S1.4
  GND: Raspberry_Pi_1.GND, J1.gnd, VCC1.-, S1.1, S1.2
  N2: Raspberry_Pi_1.GPIO18, J1.pulse
  N3: J1.vcc, VCC1.+
