# Fritzing sketch prog06_schema (saved by Fritzing 0.9.4)

parts:
  Raspberry_Pi_1 = Raspberry Pi 3 [part_number=RPI-3-V1.2]
  MOTOR1 = 28BYJ-48 Stepper Motor
  BREAKOUT1 = ULN2003A breakout board

nets:
  N1: Raspberry_Pi_1.GPIO21, BREAKOUT1.In_4
  N2: Raspberry_Pi_1.GPIO20, BREAKOUT1.In_3
  N3: Raspberry_Pi_1.GPIO16, BREAKOUT1.In_2
  N4: Raspberry_Pi_1.GPIO12, BREAKOUT1.In_1
  N5: Raspberry_Pi_1.GND, BREAKOUT1.0V
  5V: Raspberry_Pi_1.5V, BREAKOUT1.+5V
  N6: MOTOR1.RED, BREAKOUT1.RED_wire
  N7: MOTOR1.ORANGE, BREAKOUT1.ORANGE_wire
  N8: MOTOR1.YELLOW, BREAKOUT1.YELLOW_wire
  N9: MOTOR1.PINK, BREAKOUT1.PINK_wire
  N10: MOTOR1.BLUE, BREAKOUT1.BLUE_wire

custom parts:
  ULN2003A breakout board: ULN2003A 7-way Darlington Transistor Driver on breakoutboard
