# Fritzing sketch prog04_schema (saved by Fritzing 0.9.4)
breadboards: 1

parts:
  Raspberry_Pi_1 = Raspberry Pi 3 [part_number=RPI-3-V1.2]
  R1 = Temperature Sensor (Thermistor) [thermistor_type=NTC package=THT]
  R2 = Resistor [tolerance=±5% resistance=220 package="2512 [SMD]"]
  ADC1 = MCP3008 [package=dil16]
  LED1 = LED - 5mm [color="Red (633nm)" package="5 mm [THT]"]
  LED2 = LED - 5mm [color="Green (555nm)" package="5 mm [THT]"]
  LED3 = LED - 5mm [color="Yellow (595nm)" package="5 mm [THT]"]
  R3 = Resistor [tolerance=±5% resistance=220 package="2512 [SMD]"]
  R4 = Resistor [tolerance=±5% resistance=220 package="2512 [SMD]"]
  R5 = Resistor [tolerance=±5% resistance=220 package="2512 [SMD]"]

nets:
  3V3: Raspberry_Pi_1.3v3, R2.Pin_1, ADC1.VREF, ADC1.VDD
  N1: Raspberry_Pi_1.GPIO10, ADC1.Din
  N2: Raspberry_Pi_1.GPIO9, ADC1.Dout
  N3: Raspberry_Pi_1.GPIO11, ADC1.CLK
  N4: Raspberry_Pi_1.GPIO21, LED1.anode
  N5: Raspberry_Pi_1.GPIO20, LED3.anode
  N6: Raspberry_Pi_1.GPIO16, LED2.anode
  N7: Raspberry_Pi_1.GND, R1.pin_0, ADC1.DGND, ADC1.AGND, R3.Pin_0, R4.Pin_0, R5.Pin_0
  N8: Raspberry_Pi_1.GPIO8, ADC1.CS/SHDN
  N9: R1.pin_1, R2.Pin_0, ADC1.CH7
  N10: LED1.cathode, R3.Pin_1
  N11: LED2.cathode, R5.Pin_1
  N12: LED3.cathode, R4.Pin_1
