# Fritzing sketch prog05_schema (saved by Fritzing 0.9.4)
breadboards: 1

parts:
  Raspberry_Pi_1 = Raspberry Pi 3 [part_number=RPI-3-V1.2]
  R1 = Temperature Sensor (Thermistor) [thermistor_type=NTC package=THT]
  R2 = Resistor [tolerance=±5% resistance=220 package="2512 [SMD]"]
  ADC1 = MCP3008 [package=dil16]
  S1 = Pushbutton [package="[SMD]"]

nets:
  3V3: Raspberry_Pi_1.3v3, R2.Pin_1, ADC1.VREF, ADC1.VDD
  N1: Raspberry_Pi_1.GPIO2, S1.Pin_3, S1.Pin_4
  N2: Raspberry_Pi_1.GPIO10, ADC1.Din
  N3: Raspberry_Pi_1.GPIO9, ADC1.Dout
  N4: Raspberry_Pi_1.GPIO11, ADC1.CLK
  N5: Raspberry_Pi_1.GPIO8, ADC1.CS/SHDN
  N6: Raspberry_Pi_1.GND, R1.pin_0, ADC1.DGND, ADC1.AGND, S1.Pin_1, S1.Pin_2
  N7: R1.pin_1, R2.Pin_0, ADC1.CH7
