# Fritzing sketch prog06_schema (saved by Fritzing 0.9.4)
breadboards: 1

parts:
  Raspberry_Pi_1 = Raspberry Pi 3 [part_number=RPI-3-V1.2]
  IC1 = L293D [package=THT]
  M1 = DC Motor
  VCC1 = 4 x AAA Battery Mount
  DHT1 = DHT11 Humitidy and Temperature Sensor
  R1 = Resistor [tolerance=±5% resistance=220 package="2010 [SMD]"]

nets:
  3V3: Raspberry_Pi_1.3v3, IC1.+V, DHT1.VDD, R1.Pin_1
  N1: Raspberry_Pi_1.GPIO3, DHT1.DATA, R1.Pin_0
  N2: Raspberry_Pi_1.GIPO25, IC1.Enable_1
  N3: Raspberry_Pi_1.GIPO24, IC1.In_1
  N4: Raspberry_Pi_1.GIPO23, IC1.In_2
  GND: Raspberry_Pi_1.GND, IC1.0V, VCC1.-, DHT1.GND
  N5: IC1.Out_1_(_Controlled_by_Enable_1_), M1.pin_2
  N6: IC1.Out_2_(_Controlled_by_Enable_1_), M1.pin_1
  N7: IC1.+Vmotor, VCC1.+

custom parts:
  DHT11 Humitidy and Temperature Sensor: DHT11 Humidity and Temperature Sensor
