# Fritzing sketch prog01_schema (saved by Fritzing 0.9.4)
breadboards: 1

parts:
  Raspberry_Pi_1 = Raspberry Pi 3 [part_number=RPI-3-V1.2]
  ADC1 = MCP3008 [package=dil16]
  U1 = LM 358 Dual Op-Amp [package="DIP8 [THT]"]
  P1 = S1133 Si Photodiode [package="8mm Ceramic [THT]"]
  R1 = Resistor [tolerance=±5% resistance=220 package="0603 [SMD]"]
  R2 = Resistor [tolerance=±5% resistance=220 package="0603 [SMD]"]
  R3 = Resistor [tolerance=±5% resistance=220 package="0603 [SMD]"]

nets:
  3V3: Raspberry_Pi_1.3v3, ADC1.VREF, ADC1.VDD, U1.connector7
  N1: Raspberry_Pi_1.GPIO10, ADC1.Din
  N2: Raspberry_Pi_1.GPIO9, ADC1.Dout
  N3: Raspberry_Pi_1.GPIO11, ADC1.CLK
  N4: Raspberry_Pi_1.GPIO8, ADC1.CS/SHDN
  N5: Raspberry_Pi_1.GND, ADC1.DGND, ADC1.AGND, U1.connector3, U1.connector4, P1.anode, R3.Pin_1
  N6: ADC1.CH7, U1.connector0, R2.Pin_0
  N7: U1.connector1, R2.Pin_1, R3.Pin_0
  N8: U1.connector2, U1.connector6
  N9: U1.connector5, P1.cathode, R1.Pin_1
