# Fritzing sketch prog01_IRLED (saved by Fritzing 0.9.4)
breadboards: 1

parts:
  Raspberry_Pi_1 = Raspberry Pi 3 [part_number=RPI-3-V1.2]
  R1 = Resistor [tolerance=±5% resistance=220 package="0402 [SMD]"]
  D1 = LTE-302 [package=lte-302]

nets:
  N1: Raspberry_Pi_1.GPIO17, R1.Pin_0
  N2: Raspberry_Pi_1.GND, D1.C
  N3: R1.Pin_1, D1.A
